// Digital circuit control.dig as structural Verilog
module control (
  input  [15:0] Instr,
  output [3:0] RT,
  output RTW,
  output [7:0] Imm,
  output LoD
);

  assign RT = LoD ? Instr[11:8] : 4'bz;  // Driver driver_1
  assign Imm = LoD ? Instr[7:0] : 8'bz;  // Driver driver_2
  Decoder #(.Selector_Bits(4)) decoder_1 (
    .sel(Instr[15:12]), .out_2(LoD));  // open: out_0, out_1, out_3, out_4, out_5, out_6, out_7, out_8, out_9, out_10, out_11, out_12, out_13, out_14, out_15

  assign RTW = LoD;

  // Other names for the same wires on the sheet: _0_7Imm = LoD; _8_11RT = LoD

  // Notes on the sheet:
  //   RT: Address of target register
  //   RTW: Address of target register
  //   Imm: 8 bit immediate value
  //   LoD: Write target with low bits set to Imm to data
endmodule
